# Fritzing sketch LoLin-alarm-BMP180-DHT11 (saved by Fritzing 0.9.2b)
circuit board: 8.46667cm x 5.64444cm
breadboards: 2

parts:
  LED1 = LED - 5mm [color="Blue (505nm)" package="5 mm [THT]"]
  R1 = Resistor [tolerance=±5% resistance=120 package=THT]
  LED2 = LED - 5mm [color="Red (633nm)" package="5 mm [THT]"]
  R2 = Resistor [tolerance=±5% resistance=120 package=THT]
  Part1 = nodeMCU LoLin
  PIR1 = PIR sensor
  PIR2 = PIR sensor
  PIR3 = PIR sensor
  DHT1 = DHT11 Humitidy and Temperature Sensor  # not connected
  BMP1 = BMP085 Breakout  # not connected
  Part2 = Breadboard Power Supply Board SMD  # not connected
  U1 = V_REG_MC33269 [part_number=3.3V package=dpak]  # not connected

nets:
  N1: LED1.cathode, LED2.cathode, Part1.S3, Part1.GND#32
  N2: LED1.anode, R1.Pin_1
  N3: R1.Pin_0, Part1.D4
  N4: LED2.anode, R2.Pin_1
  N5: R2.Pin_0, Part1.D3
  N6: Part1.VU, Part1.D10
  GND: Part1.GND#29, PIR1.GND, PIR2.GND, PIR3.GND

custom parts:
  nodeMCU LoLin: LoLin is a tiny board, based on ESP8266, integates GPIO, PWM, IIC, 1-Wire and ADC all in one board. It's base on NodeMCU, A lua based firmware for wifi-soc esp8266 Build on ESP8266 sdk Lua core based on eLua project cjson based on lua-cjson File system based on spiffs Easy to access wireless router Based on Lua 5.1.4 (without debug, os module.) Event-Drive programming preferred. Build-in json,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
  DHT11 Humitidy and Temperature Sensor: DHT11 Humidity and Temperature Sensor
  BMP085 Breakout: A breakout for the BMP085 barometric pressure and temperature sensor
